# Fritzing sketch schematic (saved by Fritzing 0.9.10b)
breadboards: 1

parts:
  Part1 = Adafruit HUZZAH32 ESP32 Feather [part_number="Adafruit #3405"]
  RE1 = Rotary Encoder [package=THT]
  RE2 = Rotary Encoder [package=THT]
  RE3 = Rotary Encoder [package=THT]
  RE4 = Rotary Encoder [package=THT]
  Part2 = 12 NeoPixel Ring [part_number=1643]
  R1 = Slide Potentiometer [maximum_resistance=100kΩ knob_status=50% power=0.5W]  # not connected
  ENCODER1 = Rotary Encoder with Knob  # not connected

nets:
  N1: Part1.A4_IO36, RE4.EncoderPinC
  N2: Part1.A3_I39, RE3.EncoderPinC
  N3: Part1.A2_I34, RE2.EncoderPinC
  N4: Part1.A1_DAC1, RE1.EncoderPinC
  GND: Part1.GND, RE1.EncoderPinA, RE2.EncoderPinA, RE3.EncoderPinA, RE4.EncoderPinA, Part2.GND
  3.3V: Part1.3.3V, RE1.EncoderPinB, RE2.EncoderPinB, RE3.EncoderPinB, RE4.EncoderPinB, Part2.VDD
  N5: Part1.IO15_A8, Part2.IN

custom parts:
  12 NeoPixel Ring: 12 ultra bright smart LED NeoPixels are arranged in a circle with 1.5" (37mm) outer diameter. The rings are 'chainable' - connect the output pin of one to the input pin of another. Use only one microcontroller pin to control as many as you can chain together! Each LED is addressable as the driver chip is inside the LED. Each one has ~18mA constant current drive so the color will be very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
  Rotary Encoder with Knob: Rotary Encoder with 1/4" Shaft and Knob
