# Fritzing sketch schematic (saved by Fritzing 0.9.10b)
breadboards: 1

parts:
  Part1 = Adafruit HUZZAH32 ESP32 Feather [part_number="Adafruit #3405"]
  RE1 = Rotary Encoder [package=THT]
  RE2 = Rotary Encoder [package=THT]
  RE3 = Rotary Encoder [package=THT]
  RE4 = Rotary Encoder [package=THT]
  Part2 = 12 NeoPixel Ring [part_number=1643]
  R1 = Slide Potentiometer [maximum_resistance=100kΩ knob_status=50% power=0.5W]
  ENCODER1 = Rotary Encoder with Knob

nets (from the breadboard view):
  N1: Part1.A4_IO36, RE4.EncoderPinA
  N2: Part1.A3_I39, RE3.EncoderPinA
  N3: Part1.A2_I34, RE2.EncoderPinA
  GND: Part1.GND, RE1.EncoderPinC, RE2.EncoderPinC, RE3.EncoderPinC, RE4.EncoderPinC, Part2.GND, R1.wiper, ENCODER1.no_name_yet#2, ENCODER1.no_name_yet#5
  3.3V: Part1.3.3V, RE1.EncoderPinB, RE2.EncoderPinB, RE3.EncoderPinB, RE4.EncoderPinB, Part2.VDD, R1.leg2
  N4: Part1.IO13_A12, ENCODER1.no_name_yet#4
  N5: Part1.IO12_A11, ENCODER1.no_name_yet#1
  N6: Part1.IO33_A9, RE1.EncoderPinA
  N7: Part1.IO15_A8, Part2.IN
  N8: Part1.IO32_A7, R1.leg1
  N9: Part1.IO14_A6, ENCODER1.no_name_yet#3

custom parts:
  12 NeoPixel Ring: 12 ultra bright smart LED NeoPixels are arranged in a circle with 1.5" (37mm) outer diameter. The rings are 'chainable' - connect the output pin of one to the input pin of another. Use only one microcontroller pin to control as many as you can chain together! Each LED is addressable as the driver chip is inside the LED. Each one has ~18mA constant current drive so the color will be very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
  Rotary Encoder with Knob: Rotary Encoder with 1/4" Shaft and Knob
